// Logisim project 4-bit ALU.circ as structural Verilog
module ALU4Bit (
  input  [3:0] C,
  input  [3:0] A,
  input  [3:0] B,
  output Overflow,
  output [3:0] R,
  output Zero
);

  wire alu1bit_1_carryout, alu1bit_2_carryout, alu1bit_3_carryout, alu1bit_4_set, and_1_out, and_3_out,
       and_4_out, issame_1_issame, issame_2_issame, nor_1_out, or_1_out, or_2_out, xor_1_out, xor_2_out;

  // Probe on A
  // Probe on B
  or or_1 (or_1_out, alu1bit_4_set, nor_1_out);
  and and_1 (and_1_out, ~C[3], C[2]);  // AND_Gate
  ALU1Bit alu1bit_1 (
    .Operation(C[1:0]), .CarryOut(alu1bit_1_carryout), .CarryIn(and_1_out), .Result(R[0]), .A(A[0]),
    .AInvert(C[3]), .BInvert(C[2]), .B(B[0]), .Less(or_1_out));  // open: Set
  ALU1Bit alu1bit_2 (
    .Operation(C[1:0]), .CarryOut(alu1bit_2_carryout), .CarryIn(alu1bit_1_carryout), .Result(R[1]), .A(A[1]),
    .AInvert(C[3]), .BInvert(C[2]), .B(B[1]));  // open: Less, Set
  ALU1Bit alu1bit_3 (
    .Operation(C[1:0]), .CarryOut(alu1bit_3_carryout), .CarryIn(alu1bit_2_carryout), .Result(R[2]), .A(A[2]),
    .AInvert(C[3]), .BInvert(C[2]), .B(B[2]));  // open: Less, Set
  ALU1Bit alu1bit_4 (
    .Operation(C[1:0]), .CarryIn(alu1bit_3_carryout), .Result(R[3]), .A(A[3]), .AInvert(C[3]),
    .BInvert(C[2]), .B(B[3]), .Set(alu1bit_4_set));  // open: CarryOut, Less
  // Probe on R
  and and_2 (Zero, ~R[3], ~R[2], ~R[1], ~R[0]);  // AND_Gate
  and and_3 (and_3_out, ~C[0], C[1], ~C[2], ~C[3]);  // AND_Gate
  or or_2 (or_2_out, and_3_out, and_4_out);
  and and_4 (and_4_out, ~C[0], C[1], C[2], ~C[3]);  // AND_Gate
  and and_5 (Overflow, or_2_out, nor_1_out);
  nor nor_1 (nor_1_out, issame_1_issame, issame_2_issame);
  isSame issame_1 (.isSame(issame_1_issame), .B(xor_1_out), .A(R[3]));
  xor xor_1 (xor_1_out, A[3], C[3]);
  isSame issame_2 (.isSame(issame_2_issame), .B(xor_2_out), .A(R[3]));
  xor xor_2 (xor_2_out, B[3], C[2]);

  // Notes on the sheet:
  //   Milan Singh - 2606543803
endmodule

module ALU1Bit (
  input  AInvert,
  input  BInvert,
  input  CarryIn,
  input  [1:0] Operation,
  input  A,
  input  B,
  input  Less,
  output Result,
  output Set,
  output CarryOut
);

  wire and_1_out, or_1_out, xor_1_out, xor_2_out;

  xor xor_1 (xor_1_out, AInvert, A);
  xor xor_2 (xor_2_out, BInvert, B);
  and and_1 (and_1_out, xor_1_out, xor_2_out);
  or or_1 (or_1_out, xor_1_out, xor_2_out);
  Add add_1 (.Cout(CarryOut), .Sum(Set), .B(xor_2_out), .A(xor_1_out), .Cin(CarryIn));
  Mux mux_1 (.S0(Operation[0]), .S1(Operation[1]), .D3(Less), .D2(Set), .D1(or_1_out), .D0(and_1_out), .out_7(Result));

  // Notes on the sheet:
  //   Milan Singh - 2606543803
endmodule

module Add (
  input  Cin,
  input  A,
  input  B,
  output Sum,
  output Cout
);

  wire halfadder_1_carry, halfadder_1_sum, halfadder_2_carry;

  halfAdder halfadder_1 (.A(A), .B(B), .Sum(halfadder_1_sum), .Carry(halfadder_1_carry));
  halfAdder halfadder_2 (.A(Cin), .B(halfadder_1_sum), .Sum(Sum), .Carry(halfadder_2_carry));
  or or_1 (Cout, halfadder_2_carry, halfadder_1_carry);

  // Notes on the sheet:
  //   Milan Singh - 2606543803
endmodule

module Decode (
  input  S0,
  input  S1,
  output D0,
  output D1,
  output D2,
  output D3
);

  and and_1 (D0, ~S0, ~S1);  // AND_Gate
  and and_2 (D1, S0, ~S1);  // AND_Gate
  and and_3 (D2, ~S0, S1);  // AND_Gate
  and and_4 (D3, S0, S1);

  // Notes on the sheet:
  //   Milan Singh - 2606543803
endmodule

module Mux (
  input  D3,
  input  D2,
  input  D1,
  input  D0,
  input  S0,
  input  S1,
  output out_7
);

  wire and_1_out, and_2_out, and_3_out, and_4_out, decode_1_d0, decode_1_d1, decode_1_d2, decode_1_d3;

  Decode decode_1 (.S0(S0), .S1(S1), .D0(decode_1_d0), .D1(decode_1_d1), .D2(decode_1_d2), .D3(decode_1_d3));
  and and_1 (and_1_out, decode_1_d3, D3);
  and and_2 (and_2_out, decode_1_d2, D2);
  or or_1 (out_7, and_1_out, and_2_out, and_3_out, and_4_out);
  and and_3 (and_3_out, decode_1_d1, D1);
  and and_4 (and_4_out, decode_1_d0, D0);

  // Notes on the sheet:
  //   Milan Singh - 2606543803
endmodule

module halfAdder (
  input  A,
  input  B,
  output Sum,
  output Carry
);

  xor xor_1 (Sum, A, B);
  and and_1 (Carry, B, A);

  // Notes on the sheet:
  //   Milan Singh - 2606543803
endmodule

module isSame (
  input  A,
  input  B,
  output isSame
);

  wire and_1_out, and_2_out;

  and and_1 (and_1_out, A, B);
  and and_2 (and_2_out, ~A, ~B);  // AND_Gate
  or or_1 (isSame, and_1_out, and_2_out);

  // Notes on the sheet:
  //   Milan Singh - 2606543803
endmodule
